# Fritzing sketch shellGame (saved by Fritzing 0.8.5b)
breadboards: 1

parts:
  Part1 = Arduino Uno (Rev3)
  R1 = Resistor [tolerance=±5% resistance=330 package=THT]
  S1 = Pushbutton [package="[THT]"]
  R2 = Resistor [tolerance=±5% resistance=10k package=THT]
  LED1 = LED - 5mm [color="Yellow (595nm)" package="5 mm [THT]"]
  LED2 = LED - 5mm [color="Red (633nm)" package="5 mm [THT]"]
  R3 = Resistor [tolerance=±5% resistance=330 package=THT]
  S2 = Pushbutton [package="[THT]"]
  R4 = Resistor [tolerance=±5% resistance=10k package=THT]
  LED3 = LED - 5mm [color="Yellow (595nm)" package="5 mm [THT]"]
  R5 = Resistor [tolerance=±5% resistance=330 package=THT]
  S3 = Pushbutton [package="[THT]"]
  R6 = Resistor [tolerance=±5% resistance=10k package=THT]
  J1 = Piezo Speaker

nets:
  N1: Part1.D8, S3.Pin_3, S3.Pin_4, R6.Pin_1
  N2: Part1.D9_PWM, J1.pin2
  N3: Part1.GND, R1.Pin_0, R2.Pin_0, R3.Pin_0, R4.Pin_0, R5.Pin_0
  N4: Part1.D2, LED1.cathode
  N5: Part1.D3_PWM, S1.Pin_3, S1.Pin_4, R2.Pin_1
  N6: Part1.D4, LED2.cathode
  N7: Part1.D5_PWM, S2.Pin_3, S2.Pin_4, R4.Pin_1
  N8: Part1.D6_PWM, LED3.cathode
  N9: Part1.5V, S1.Pin_1, S1.Pin_2, S2.Pin_1, S2.Pin_2, S3.Pin_1, S3.Pin_2
  N10: R1.Pin_1, LED1.anode
  N11: LED2.anode, R3.Pin_1
  N12: LED3.anode, R5.Pin_1
